// Logisim project masina_spalat.circ as structural Verilog
module test (
  input  Input_1,
  input  Input_2,
  input  [1:0] Input_bus_1,
  input  [2:0] Input_bus_2,
  input  [1:0] Input_bus_3,
  input  [1:0] Input_bus_4,
  input  Input_3,
  input  Input_4,
  output [3:0] Output_bus_1
);

  wire Button_1_out, Button_2_out, Button_3_out, Clk_1_sec, numarator_1min_1_fin, numarator_timp_total_1_fin,
       pornire, Reset, selecteaza_mod_1_mod_automat, selecteaza_mod_1_mod_manual, Start,
       unitate_control_1_as_mod_spalare, unitate_control_1_astept_usa_led, unitate_control_1_blocare_usa,
       unitate_control_1_enable_cnt_1, unitate_control_1_enable_cnt_total, unitate_control_1_final;
  wire [1:0] divizor_frecventa_1_selectie;
  wire [3:0] binary_to_decimal_converter_1_decimal, binary_to_decimal_converter_1_mii,
       binary_to_decimal_converter_1_sute, binary_to_decimal_converter_1_unit, mux4_1_1_output;
  wire [6:0] decodificator_7segmente_1_output;
  wire [11:0] alu_timp_manual_1_output, mux2_1_12biti_1_output, numarator_timp_total_1_output,
       rom_moduri_1_iesire_tmp, rom_temperatura_1_iesire_temp;

  Button Button_1 (.out(Button_1_out));
  Button Button_2 (.out(Button_2_out));
  Button Button_3 (.out(Button_3_out));
  Selecteaza_mod selecteaza_mod_1 (
    .reset(Reset), .mod_s(Input_bus_1), .mod_automat(selecteaza_mod_1_mod_automat),
    .mod_manual(selecteaza_mod_1_mod_manual));
  debouncer debouncer_1 (.buton(Button_1_out), .clk(Input_1), .iesire(Start));
  debouncer debouncer_2 (.buton(Button_2_out), .clk(Input_1), .iesire(Reset));
  debouncer debouncer_3 (.buton(Button_3_out), .clk(Input_1), .iesire(pornire));
  Unitate_Control unitate_control_1 (
    .clk(Clk_1_sec), .reset(Reset), .inchide_usa(Input_2), .Start(Start), .pornire(pornire),
    .Enable_automat(selecteaza_mod_1_mod_automat), .Enable_manual(selecteaza_mod_1_mod_manual),
    .fin_cnt_total(numarator_timp_total_1_fin), .fin_cnt_1(numarator_1min_1_fin),
    .enable_cnt_total(unitate_control_1_enable_cnt_total), .enable_cnt_1(unitate_control_1_enable_cnt_1),
    .as_mod_spalare(unitate_control_1_as_mod_spalare), .astept_usa_led(unitate_control_1_astept_usa_led),
    .blocare_usa(unitate_control_1_blocare_usa), .\final (unitate_control_1_final));
  rom_moduri rom_moduri_1 (
    .Select_mod(Input_bus_2), .Enable(selecteaza_mod_1_mod_automat), .Iesire_tmp(rom_moduri_1_iesire_tmp));
  rom_temperatura rom_temperatura_1 (
    .Select_temp(Input_bus_3), .Enable(selecteaza_mod_1_mod_manual),
    .iesire_temp(rom_temperatura_1_iesire_temp));
  rom_viteze rom_viteze_1 (.Enable(selecteaza_mod_1_mod_manual), .Sel_vit(Input_bus_4));  // open: iesire_vit
  LED Astept_mod_spalare (.in(unitate_control_1_as_mod_spalare));
  LED Astept_usa (.in(unitate_control_1_astept_usa_led));
  LED Blocare_usa (.in(unitate_control_1_blocare_usa));
  LED Final (.in(unitate_control_1_final));
  divizor_frec_1sec divizor_frec_1sec_1 (.clk(Input_1), .reset(Reset), .clk_1sec(Clk_1_sec));
  ALU_Timp_Manual alu_timp_manual_1 (
    .\input (rom_temperatura_1_iesire_temp), .enable(selecteaza_mod_1_mod_manual), .prespalare(Input_3),
    .clatire_suplimentara(Input_4), .\output (alu_timp_manual_1_output));
  Mux2_1_12biti mux2_1_12biti_1 (
    .input1(rom_moduri_1_iesire_tmp), .input2(alu_timp_manual_1_output), .sel(Input_bus_1),
    .\output (mux2_1_12biti_1_output));
  Numarator_timp_total numarator_timp_total_1 (
    .\input (mux2_1_12biti_1_output), .clk(Clk_1_sec), .reset(Reset),
    .enable(unitate_control_1_enable_cnt_total), .\output (numarator_timp_total_1_output),
    .fin(numarator_timp_total_1_fin));
  Numarator_1min numarator_1min_1 (
    .clk(Clk_1_sec), .reset(Reset), .enable(unitate_control_1_enable_cnt_1), .fin(numarator_1min_1_fin));  // open: output
  Binary_to_decimal_converter binary_to_decimal_converter_1 (
    .Bin_num(numarator_timp_total_1_output), .Unit(binary_to_decimal_converter_1_unit),
    .Decimal(binary_to_decimal_converter_1_decimal), .sute(binary_to_decimal_converter_1_sute),
    .mii(binary_to_decimal_converter_1_mii));
  divizor_frecventa divizor_frecventa_1 (.clk(Input_1), .reset(Reset), .selectie(divizor_frecventa_1_selectie));
  MUX4_1 mux4_1_1 (
    .input1(binary_to_decimal_converter_1_unit), .input2(binary_to_decimal_converter_1_decimal),
    .input3(binary_to_decimal_converter_1_sute), .input4(binary_to_decimal_converter_1_mii),
    .sel(divizor_frecventa_1_selectie), .reset(Reset), .\output (mux4_1_1_output));
  MUX4_1_afisoare mux4_1_afisoare_1 (.sel(divizor_frecventa_1_selectie), .reset(Reset), .\output (Output_bus_1));
  decodificator_7segmente decodificator_7segmente_1 (
    .\input (mux4_1_1_output), .\output (decodificator_7segmente_1_output));
  _7_Segment_Display L_7_Segment_Display_1 (
    .g(decodificator_7segmente_1_output[0]), .f(decodificator_7segmente_1_output[1]),
    .a(decodificator_7segmente_1_output[6]), .b(decodificator_7segmente_1_output[5]),
    .e(decodificator_7segmente_1_output[2]), .d(decodificator_7segmente_1_output[3]),
    .c(decodificator_7segmente_1_output[4]), .dp(1'b0));

  // Other names for the same wires on the sheet: Clatire_sup = Input_4; clock_placuta = Input_1;
  //   Inchide_usa = Input_2; Mod_s[1:0] = Input_bus_1; Prespalare = Input_3;
  //   Selecteaza_mod_automat[2:0] = Input_bus_2; Selecteaza_temp[1:0] = Input_bus_3;
  //   Selecteaza_viteza[1:0] = Input_bus_4
endmodule

// VHDL entity rom_viteze, as the project stores it:
--------------------------------------------------------------------------------
-- Project :
-- File    :
-- Autor   :
-- Date    :
--
--------------------------------------------------------------------------------
-- Description :
--
--------------------------------------------------------------------------------

LIBRARY ieee;
USE ieee.std_logic_1164.all;

use ieee.std_logic_unsigned.all;
use ieee.numeric_std.all;

ENTITY rom_viteze IS
  PORT (
  Enable: in std_logic;	--enable
  Sel_vit: in std_logic_vector (1 downto 0);
  iesire_vit: out std_logic_vector(1 downto 0)
    );
END rom_viteze;

--------------------------------------------------------------------------------
--Complete your VHDL description below
--------------------------------------------------------------------------------

ARCHITECTURE TypeArchitecture OF rom_viteze IS

type matrice is array (0 to 3) of std_logic_vector(0 to 1);
BEGIN

process(sel_vit, enable)
variable mem: matrice:=(
"00",
"01",
"10",
"11");
begin

if enable='0' then iesire_vit<="11";
else iesire_vit<=mem(conv_integer(sel_vit));
end if;
end process;
END TypeArchitecture;

// VHDL entity rom_moduri, as the project stores it:
--------------------------------------------------------------------------------
-- Project :
-- File    :
-- Autor   :
-- Date    :
--
--------------------------------------------------------------------------------
-- Description :
--
--------------------------------------------------------------------------------

LIBRARY ieee;
USE ieee.std_logic_1164.all;
use ieee.std_logic_unsigned.all;
use ieee.numeric_std.all;
ENTITY rom_moduri IS
  PORT (
  	Select_mod: in std_logic_vector(2 downto 0);			--verificam care intrare e
  	Enable: in std_logic;						--enable 
  	Iesire_tmp: out std_logic_vector(11 downto 0)

    );
END rom_moduri;

--------------------------------------------------------------------------------
--Complete your VHDL description below
--------------------------------------------------------------------------------

ARCHITECTURE TypeArchitecture OF rom_moduri IS

type MATRICE is array(0 to 7) of std_logic_vector(0 to 11);
BEGIN
process(Select_mod,Enable)
variable mem: MATRICE:=(
"100101111110",			
"100110111010",
"100110010010",
"101111101010",
"110001001110",
"000000000000",
"000000000000",
"000000000000");
begin
if Enable='0' then Iesire_tmp<="000000000000";
else 
Iesire_tmp<=mem(conv_integer(Select_mod));
end if;
end process;
END TypeArchitecture;

// VHDL entity rom_temperatura, as the project stores it:
--------------------------------------------------------------------------------
-- Project :
-- File    :
-- Autor   :
-- Date    :
--
--------------------------------------------------------------------------------
-- Description 
--
--------------------------------------------------------------------------------

LIBRARY ieee;
USE ieee.std_logic_1164.all;
use ieee.std_logic_unsigned.all;
use ieee.numeric_std.all;
ENTITY rom_temperatura IS
  PORT (
  	Select_temp: in std_logic_vector(1 downto 0);
  	Enable: in std_logic;						
  	iesire_temp: out std_logic_vector(11 downto 0)	
    );
END rom_temperatura;

--------------------------------------------------------------------------------
--Complete your VHDL description below
--------------------------------------------------------------------------------

ARCHITECTURE TypeArchitecture OF rom_temperatura IS

type MATRICE is array(0 to 3) of std_logic_vector(0 to 11);
BEGIN

process(Select_temp, Enable)
variable mem: MATRICE:=(
"100101111110",			
"100110010010",
"100110111010",
"100111110110");
begin
if Enable='0' then iesire_temp<="000000000000";
else 
iesire_temp<=mem(conv_integer(Select_temp));
end if;

end process;
END TypeArchitecture;

// VHDL entity ALU_Timp_Manual, as the project stores it:
--------------------------------------------------------------------------------
-- Project :
-- File    :
-- Autor   :
-- Date    :
--
--------------------------------------------------------------------------------
-- Description :
--
--------------------------------------------------------------------------------

LIBRARY ieee;
USE ieee.std_logic_1164.all;
USE ieee.std_logic_arith.all;
USE ieee.std_logic_unsigned.all;
ENTITY ALU_Timp_Manual IS
  PORT (
  input: in std_logic_vector(11 downto 0);
  enable: in std_logic;
  prespalare, clatire_suplimentara: in std_logic;
  output: out std_logic_vector(11 downto 0)
  
    );
END ALU_Timp_Manual;

--------------------------------------------------------------------------------
--Complete your VHDL description below
--------------------------------------------------------------------------------

ARCHITECTURE TypeArchitecture OF ALU_Timp_Manual IS
BEGIN
process(enable, input, prespalare, clatire_suplimentara)
variable var: std_logic_vector(11 downto 0);
begin
if(enable='1') then
   var:=input;
   if(prespalare='1') then
   var:=var+"001001011000";
   end if;
   if(clatire_suplimentara='1') then
   var:=var+"001001011000";
   end if;
else var:="000000000000";
end if;
output<=var;
end process;
END TypeArchitecture;

// VHDL entity Selecteaza_mod, as the project stores it:
--------------------------------------------------------------------------------
-- Project :
-- File    :
-- Autor   :
-- Date    :
--
--------------------------------------------------------------------------------
-- Description :
--
--------------------------------------------------------------------------------

LIBRARY ieee;
USE ieee.std_logic_1164.all;

ENTITY Selecteaza_mod IS
  PORT (
          reset: in std_logic; 
          mod_s: in std_logic_vector(1 downto 0);
          mod_automat, mod_manual: out std_logic 
    );
END Selecteaza_mod;

--------------------------------------------------------------------------------
--Complete your VHDL description below
--------------------------------------------------------------------------------

ARCHITECTURE TypeArchitecture OF Selecteaza_mod IS

BEGIN
process(mod_s, reset)
begin
if(reset='1') then mod_automat<='0';
mod_manual<='0';
else
case mod_s is 
when "10"=> mod_automat<='1';
           mod_manual<='0';
when "01"=> mod_automat<='0';
mod_manual<='1';
when others=> mod_automat<='0';
mod_manual<='0';
 
end case;
end if;
end process;
END TypeArchitecture;

// VHDL entity Mux2_1_12biti, as the project stores it:
--------------------------------------------------------------------------------
-- Project :
-- File    :
-- Autor   :
-- Date    :
--
--------------------------------------------------------------------------------
-- Description :
--
--------------------------------------------------------------------------------

LIBRARY ieee;
USE ieee.std_logic_1164.all;

ENTITY Mux2_1_12biti IS
  PORT ( 
  input1, input2:in std_logic_vector(11 downto 0);
  sel:in std_logic_vector(1 downto 0);
  output:out std_logic_vector(11 downto 0)
    );
END Mux2_1_12biti;

--------------------------------------------------------------------------------
--Complete your VHDL description below
--------------------------------------------------------------------------------

ARCHITECTURE TypeArchitecture OF Mux2_1_12biti IS

BEGIN
process(sel, input1, input2)
begin
case sel is 
when "01" => output<=input2;
when "10" => output<=input1;
when others => output<="000000000000";
end case;
end process;
END TypeArchitecture;

// VHDL entity Numarator_timp_total, as the project stores it:
--------------------------------------------------------------------------------
-- Project :
-- File    :
-- Autor   :
-- Date    :
--
--------------------------------------------------------------------------------
-- Description :
--
--------------------------------------------------------------------------------

LIBRARY ieee;
USE ieee.std_logic_1164.all;
USE ieee.std_logic_arith.all;
USE ieee.std_logic_unsigned.all;
ENTITY Numarator_timp_total IS
  PORT (input:in std_logic_vector(11 downto 0);
        clk, reset:in std_logic;
        output:out std_logic_vector(11 downto 0);
        fin: out std_logic;
        enable: in std_logic
    );
END Numarator_timp_total;

--------------------------------------------------------------------------------
--Complete your VHDL description below
--------------------------------------------------------------------------------

ARCHITECTURE TypeArchitecture OF Numarator_timp_total IS
begin
process(clk, enable, reset, input)
variable cnt_total: std_logic_vector(11 downto 0);
begin
 if(reset = '1') then cnt_total:=input;
  elsif( rising_edge(clk)) then 
       if(cnt_total="000000000000") then fin<='1';
       else fin<='0';
       end if;
       if (enable='1') then  
       if (cnt_total/="000000000000") then cnt_total:=cnt_total-1;
       end if;
       else cnt_total:=input;
       end if;
       end if;
       output<=cnt_total;
end process;


END TypeArchitecture;

// VHDL entity Dmux4_1, as the project stores it:
--------------------------------------------------------------------------------
-- Project :
-- File    :
-- Autor   :
-- Date    :
--
--------------------------------------------------------------------------------
-- Description :
--
--------------------------------------------------------------------------------

LIBRARY ieee;
USE ieee.std_logic_1164.all;

ENTITY Dmux4_1 IS
  PORT ( output1, output2, output3, output4: out std_logic;
         sel:in std_logic_vector(1 downto 0);
         enable: in std_logic
    );
END Dmux4_1;

--------------------------------------------------------------------------------
--Complete your VHDL description below
--------------------------------------------------------------------------------

ARCHITECTURE TypeArchitecture OF Dmux4_1 IS

BEGIN
process(enable, sel)
begin
if(enable='0') then
output1<='0';
output2<='0';
output3<='0';
output4<='0';
else
if(sel="00") then output1<='1';
else output1<='0';
end if;
if(sel="01") then output2<='1';
else output2<='0';
end if;
if(sel="10") then output3<='1';
else output3<='0';
end if;
if(sel="11") then output4<='1';
else output4<='0';
end if;
end if;

end process;

END TypeArchitecture;

// VHDL entity Dmux8_1, as the project stores it:
--------------------------------------------------------------------------------
-- Project :
-- File    :
-- Autor   :
-- Date    :
--
--------------------------------------------------------------------------------
-- Description :
--
--------------------------------------------------------------------------------

LIBRARY ieee;
USE ieee.std_logic_1164.all;

ENTITY Dmux8_1 IS
  PORT (
 output1, output2, output3, output4, output5, output6, output7, output8: out std_logic;
         sel:in std_logic_vector(2 downto 0);
         enable: in std_logic
    );
END Dmux8_1;

--------------------------------------------------------------------------------
--Complete your VHDL description below
--------------------------------------------------------------------------------

ARCHITECTURE TypeArchitecture OF Dmux8_1 IS

BEGIN
process(enable, sel)
begin
if(enable='0') then
output1<='0';
output2<='0';
output3<='0';
output4<='0';
output5<='0';
output6<='0';
output7<='0';
output8<='0';
else
if(sel="000") then output1<='1';
else output1<='0';
end if;
if(sel="001") then output2<='1';
else output2<='0';
end if;
if(sel="010") then output3<='1';
else output3<='0';
end if;
if(sel="011") then output4<='1';
else output4<='0';
end if;
if(sel="100") then output5<='1';
else output5<='0';
end if;
if(sel="101") then output6<='1';
else output6<='0';
end if;
if(sel="110") then output7<='1';
else output7<='0';
end if;
if(sel="111") then output8<='1';
else output8<='0';
end if;
end if;


end process;

END TypeArchitecture;

// VHDL entity Numarator_1min, as the project stores it:
--------------------------------------------------------------------------------
-- Project :
-- File    :
-- Autor   :
-- Date    :
--
--------------------------------------------------------------------------------
-- Description :
--
--------------------------------------------------------------------------------

LIBRARY ieee;
USE ieee.std_logic_1164.all;
USE ieee.std_logic_arith.all;
USE ieee.std_logic_unsigned.all;
ENTITY Numarator_1min IS
  PORT (
        clk, reset:in std_logic;
        output:out std_logic_vector(7 downto 0);
        fin: out std_logic;
        enable: in std_logic
    );
END Numarator_1min;

--------------------------------------------------------------------------------
--Complete your VHDL description below
--------------------------------------------------------------------------------

ARCHITECTURE TypeArchitecture OF Numarator_1min IS

begin
process( clk, enable)
variable cnt_total: std_logic_vector(7 downto 0):="00000000";
begin
if(reset='1') then cnt_total:="00000000"; 
elsif (clk'event and clk='1') then
     if(cnt_total="00111100") then fin<='1';
     else fin<='0';
    if(enable='1') then cnt_total:=cnt_total+1;
   end if;
   end if;
   end if;
   output<=cnt_total;
end process;


END TypeArchitecture;

// VHDL entity Binary_to_decimal_converter, as the project stores it:
--------------------------------------------------------------------------------
-- Project :
-- File    :
-- Autor   :
-- Date    :
--
--------------------------------------------------------------------------------
-- Description :
--
--------------------------------------------------------------------------------

LIBRARY ieee;
USE ieee.std_logic_1164.all;
USE ieee.std_logic_unsigned.all;
USE ieee.std_logic_arith.all;

ENTITY Binary_to_decimal_converter IS
  PORT (
 Bin_num: in std_logic_vector(11 downto 0);
  		Unit: out std_logic_vector(3 downto 0);
  		Decimal: out std_logic_vector(3 downto 0); 
  		sute: out std_logic_vector(3 downto 0);
  		mii: out std_logic_vector(3 downto 0)
    );
END Binary_to_decimal_converter;

--------------------------------------------------------------------------------
--Complete your VHDL description below
--------------------------------------------------------------------------------

ARCHITECTURE comport OF Binary_to_decimal_converter IS

signal num_int: integer:=0;
signal u,z,s,m: integer:=0;
BEGIN

	num_int<=conv_integer(bin_num);
	z<=(num_int / 10) rem 10;
	u<=num_int rem 10;
	s<=(num_int/100)rem 10;
	m<=num_int/1000;
	process(u)
	begin
		case u is
		when 0 => unit <= x"0";
		when 1 => unit <= x"1";
		when 2 => unit <= x"2";
		when 3 => unit <= x"3";
		when 4 => unit <= x"4";
		when 5 => unit <= x"5";
		when 6 => unit <= x"6";
		when 7 => unit <= x"7";
		when 8 => unit <= x"8";
		when 9 => unit <= x"9";
		when others => unit <=x"f";
		end case;
	end process;
	process(z)
	begin
		case z is
		when 0 => Decimal <= x"0";
		when 1 => Decimal <= x"1";
		when 2 => Decimal <= x"2";
		when 3 => Decimal <= x"3";
		when 4 => Decimal <= x"4";
		when 5 => Decimal <= x"5";
		when 6 => Decimal <= x"6";
		when 7 => Decimal <= x"7";
		when 8 => Decimal <= x"8";
		when 9 => Decimal <= x"9";
		when others => Decimal <=x"f";
		end case;
	end process;
	process(s)
		begin
		case s is
		when 0 => sute <= x"0";
		when 1 => sute <= x"1";
		when 2 => sute <= x"2";
		when 3 => sute <= x"3";
		when 4 => sute <= x"4";
		when 5 => sute <= x"5";
		when 6 => sute <= x"6";
		when 7 => sute <= x"7";
		when 8 => sute <= x"8";
		when 9 => sute <= x"9";
		when others => sute <=x"f";
		end case;
	end process;
	process(m)
		begin
		case m is
		when 0 => mii <= x"0";
		when 1 => mii <= x"1";
		when 2 => mii <= x"2";
		when 3 => mii <= x"3";
		when 4 => mii <= x"4";
		when 5 => mii <= x"5";
		when 6 => mii <= x"6";
		when 7 => mii <= x"7";
		when 8 => mii <= x"8";
		when 9 => mii <= x"9";
		when others => mii <=x"f";
		end case;
	end process;

	
END comport;

// VHDL entity decodificator_7segmente, as the project stores it:
--------------------------------------------------------------------------------
-- Project :
-- File    :
-- Autor   :
-- Date    :
--
--------------------------------------------------------------------------------
-- Description :
--
--------------------------------------------------------------------------------

LIBRARY ieee;
USE ieee.std_logic_1164.all;

ENTITY decodificator_7segmente IS
  PORT (
 input: in std_logic_vector (3 downto 0);
         output: out std_logic_vector (6 downto 0)
    );
END decodificator_7segmente;

--------------------------------------------------------------------------------
--Complete your VHDL description below
--------------------------------------------------------------------------------

ARCHITECTURE TypeArchitecture OF decodificator_7segmente IS

BEGIN

output<="1111110" when input=x"0" else
"0110000" when input=x"1" else
"1101101" when input=x"2" else
"1111001" when input=x"3" else
"0110011" when input=x"4" else
"1011011" when input=x"5" else
"1011111" when input=x"6" else
"1110000" when input=x"7" else
"1111111" when input=x"8" else
"1111011" when input=x"9" else
"1110111" when input=x"A" else
"0011111" when input=x"B" else
"1001110" when input=x"C" else
"0111101" when input=x"D" else
"1001111" when input=x"E" else
"1000111" when input=x"F";
  	

END TypeArchitecture;

// VHDL entity Unitate_Control, as the project stores it:
--------------------------------------------------------------------------------
-- Project :
-- File    :
-- Autor   :
-- Date    :
--
--------------------------------------------------------------------------------
-- Description :
--
--------------------------------------------------------------------------------

LIBRARY ieee;
USE ieee.std_logic_1164.all;

ENTITY Unitate_Control IS
  PORT ( clk: in std_logic;  -- de la utilizator la uc
  	    reset: in std_logic;
	    inchide_usa: in std_logic;
	    Start: in std_logic;
	    pornire: in std_logic;
  	                                --de la uc la componenete si invers
  	    Enable_automat: in std_logic;
  	    Enable_manual: in std_logic;
  	    fin_cnt_total: in std_logic;
  	    fin_cnt_1: in std_logic;
  	    enable_cnt_total:out std_logic;
  	    enable_cnt_1: out std_logic;
  	    as_mod_spalare: out std_logic;
  	    astept_usa_led:out std_logic;
  	    blocare_usa: out std_logic;	
  	    final:out std_logic    

    );
END Unitate_Control;

--------------------------------------------------------------------------------
--Complete your VHDL description below
--------------------------------------------------------------------------------

ARCHITECTURE TypeArchitecture OF Unitate_Control IS
type stare_t is (Astept, AsteptMod, Astept_usa, Spalare, Astept_deblocare_usa, Final_St);
signal Stare, Nx_Stare: stare_t;
BEGIN
stare_actuala: process(clk, reset)
begin
if reset='1' then Stare<=Astept;
elsif clk'event and clk='1' then 
  Stare<=Nx_Stare;
end if;
end process;

Tranzitii: process(Stare, fin_cnt_total, fin_cnt_1, Start, Enable_automat, Enable_manual, inchide_usa, pornire)
begin
enable_cnt_total<='0';
enable_cnt_1<='0';
as_mod_spalare<='0';
astept_usa_led<='0';
blocare_usa<='0';
final<='0';

case Stare is 
  when Astept=>
  final<='1';
  if (pornire='1') then Nx_stare<=AsteptMod;
  else Nx_stare<=Astept;
  end if;
  
  when AsteptMod=>
  as_mod_spalare<='1';
  if(Enable_automat='1' or Enable_manual='1') then Nx_Stare<=Astept_usa;
  else Nx_Stare<=AsteptMod;
  end if;
  
  when Astept_usa=>
  astept_usa_led<='1';
  if(inchide_usa='1' and start='1') then Nx_Stare<=Spalare;
  else Nx_stare<=Astept_usa;
  end if;
  
  when Spalare=>
  blocare_usa<='1';
  enable_cnt_total<='1';
  if(fin_cnt_total='1') then Nx_Stare<=Astept_deblocare_usa;
  else Nx_Stare<=Spalare;
  end if;

  when Astept_deblocare_usa=>
  blocare_usa<='1';
  enable_cnt_1<='1';
  enable_cnt_total<='1';
  if(fin_cnt_1='1') then Nx_Stare<=Final_St;
  else Nx_Stare<=Astept_deblocare_usa;
  end if;

  when Final_St=>
  Final<='1';
  enable_cnt_total<='1';
  Nx_Stare<=Astept;
  when Others=> Nx_stare<=Astept;
  end case;
  end process;
END TypeArchitecture;

// VHDL entity MUX4_1, as the project stores it:
--------------------------------------------------------------------------------
-- Project :
-- File    :
-- Autor   :
-- Date    :
--
--------------------------------------------------------------------------------
-- Description :
--
--------------------------------------------------------------------------------

LIBRARY ieee;
USE ieee.std_logic_1164.all;

ENTITY MUX4_1 IS
  PORT ( input1, input2, input3, input4: in std_logic_vector(3 downto 0);
         sel: in std_logic_vector(1 downto 0);
         reset: in std_logic;
         output: out std_logic_vector(3 downto 0)
    );
END MUX4_1;

--------------------------------------------------------------------------------
--Complete your VHDL description below
--------------------------------------------------------------------------------

ARCHITECTURE TypeArchitecture OF MUX4_1 IS

BEGIN
process(reset, sel, input1, input2, input3, input4)
begin
if reset='1' then 
output<="1111";
else 
case sel is
when "00"=> output<=input1;
when "01"=> output<=input2;
when "10"=> output<=input3;
when "11"=> output<=input4;
when others=> output <="1111";
end case;
end if;
end process;



END TypeArchitecture;

// VHDL entity divizor_frecventa, as the project stores it:
--------------------------------------------------------------------------------
-- Project :
-- File    :
-- Autor   :
-- Date    :
--
--------------------------------------------------------------------------------
-- Description :
--
--------------------------------------------------------------------------------

LIBRARY ieee;
USE ieee.std_logic_1164.all;
use ieee.std_logic_unsigned.all;
use ieee.numeric_std.all;
ENTITY divizor_frecventa IS
  PORT (clk, reset: in std_logic;
        selectie: out std_logic_vector(1 downto 0)
    );
END divizor_frecventa;

--------------------------------------------------------------------------------
--Complete your VHDL description below
--------------------------------------------------------------------------------

ARCHITECTURE TypeArchitecture OF divizor_frecventa IS
signal numarator: std_logic_vector(15 downto 0):="0000000000000000";
BEGIN
process(clk, reset)
variable aux: integer:=0;
begin
if(reset='1') then numarator<="0000000000000000";
elsif (clk='1' and clk'event) then 
         aux:=conv_integer(numarator);
         if(aux=65_535) then numarator<="0000000000000000";
         else numarator<=numarator+"0000000000000001";
         end if;
selectie<=numarator(14 downto 13);
end if;
end process;


END TypeArchitecture;

// VHDL entity MUX4_1_afisoare, as the project stores it:
--------------------------------------------------------------------------------
-- Project :
-- File    :
-- Autor   :
-- Date    :
--
--------------------------------------------------------------------------------
-- Description :
--
--------------------------------------------------------------------------------

LIBRARY ieee;
USE ieee.std_logic_1164.all;

ENTITY MUX4_1_afisoare IS
  PORT (
         sel: in std_logic_vector(1 downto 0);
         reset: in std_logic;
         output: out std_logic_vector(3 downto 0)
    );
END MUX4_1_afisoare;

--------------------------------------------------------------------------------
--Complete your VHDL description below
--------------------------------------------------------------------------------

ARCHITECTURE TypeArchitecture OF MUX4_1_afisoare IS

BEGIN
process(reset, sel)
begin
if reset='1' then 
output<="1111";
else 
case sel is
when "00"=> output<="0001";
when "01"=> output<="0010";
when "10"=> output<="0100";
when "11"=> output<="1000";
when others=> output <="0000";
end case;
end if;
end process;

END TypeArchitecture;

// VHDL entity divizor_frec_1sec, as the project stores it:
--------------------------------------------------------------------------------
-- Project :
-- File    :
-- Autor   :
-- Date    :
--
--------------------------------------------------------------------------------
-- Description :
--
--------------------------------------------------------------------------------

LIBRARY ieee;
USE ieee.std_logic_1164.all;

ENTITY divizor_frec_1sec IS
  PORT ( clk, reset: in std_logic;
      	clk_1sec:out std_logic
    );
END divizor_frec_1sec;

--------------------------------------------------------------------------------
--Complete your VHDL description below
--------------------------------------------------------------------------------

ARCHITECTURE TypeArchitecture OF divizor_frec_1sec IS
signal aux: std_logic:='0';
BEGIN
clk_1sec<=aux;
process(reset, clk)
variable numb: integer:=0;
begin
 if(reset='1') then
 aux<='0';
 numb:=0;
 else if(rising_edge(clk)) then 
  	numb:=numb+1;
  	  if(numb=1_000_000) then
  	  aux<=not aux;
  	  numb:=0;
  	else null;
  	end if;
  	end if;
  	end if;
  	end process;

END TypeArchitecture;

// VHDL entity debouncer, as the project stores it:
--------------------------------------------------------------------------------
-- Project :
-- File    :
-- Autor   :
-- Date    :
--
--------------------------------------------------------------------------------
-- Description :
--
--------------------------------------------------------------------------------

LIBRARY ieee;
USE ieee.std_logic_1164.all;

ENTITY debouncer IS
  PORT ( buton, clk: in std_logic;
         iesire: out std_logic
    );
END debouncer;

--------------------------------------------------------------------------------
--Complete your VHDL description below
--------------------------------------------------------------------------------

ARCHITECTURE TypeArchitecture OF debouncer IS

BEGIN
process(buton, clk)
variable num: integer:=0;
begin 
if(buton='1') then
     if(rising_edge(clk)) then num:=num+1;
     end if;
else num:=0;
end if;
if(num>10) then iesire<='1';
else iesire<='0';
end if;
end process;  
END TypeArchitecture;
